# Fritzing sketch MFA Mikel (saved by Fritzing 0.9.3b)
breadboards: 1

parts:
  Arduino_Uno_R3 = Arduino Uno (Rev3)
  LCD_20_x4 = LCD screen
  Keypad = 4x4 Keypad [part_number=101207]
  LED1 = LED - 5mm [color="Green (560nm)" package="5 mm [THT]"]
  LED2 = LED - 5mm [color="Red (633nm)" package="5 mm [THT]"]
  I²C = LCM1602 IIC [part_number="LCM1602 IIC" chip_label="LCM1602 IIC" package="DIP (Dual Inline) [THT]"]
  Power_Supply = YwRobot Breadboard Power Supply [part_number=545043]
  Relay = KF-301 Relay [package=THT]
  RFID = RFID-RC522 [part_number=101218]
  Elektrisches_Schloss = DC Motor
  R1 = Resistor [tolerance=±5% resistance=220 package=THT]
  R2 = Resistor [tolerance=±5% resistance=220 package=THT]

nets:
  N1: Arduino_Uno_R3.A0, Keypad.8
  N2: Arduino_Uno_R3.A1, Keypad.7
  N3: Arduino_Uno_R3.A2, Keypad.6
  N4: Arduino_Uno_R3.A3, Keypad.5
  N5: Arduino_Uno_R3.A4/SDA, I²C.SDA
  N6: Arduino_Uno_R3.A5/SCL, I²C.SCL
  N7: Arduino_Uno_R3.D8, Relay.signal
  N8: Arduino_Uno_R3.D9_PWM, RFID.RST
  N9: Arduino_Uno_R3.D10_PWM/SS, RFID.SDA
  N10: Arduino_Uno_R3.D11_PWM/MOSI, RFID.MOSI
  N11: Arduino_Uno_R3.D12/MISO, RFID.MISO
  N12: Arduino_Uno_R3.D13/SCK, RFID.SCK
  GND: Arduino_Uno_R3.GND, I²C.GND, Power_Supply.GND#12, RFID.GND, R1.Pin_1, R2.Pin_1
  N13: Arduino_Uno_R3.D2, Keypad.4
  N14: Arduino_Uno_R3.D3_PWM, Keypad.3
  N15: Arduino_Uno_R3.D4, Keypad.2
  N16: Arduino_Uno_R3.D5_PWM, Keypad.1
  N17: Arduino_Uno_R3.D6_PWM, LED1.anode
  N18: Arduino_Uno_R3.D7, LED2.cathode, LED2.anode, R1.Pin_0
  5V: Arduino_Uno_R3.5V, I²C.VCC, Power_Supply.VCC#6
  VIN: Arduino_Uno_R3.VIN, RFID.3.3V
  VSS: LCD_20_x4.VSS, I²C.VSS
  VDD: LCD_20_x4.VDD, I²C.VDD
  N19: LCD_20_x4.V0, I²C.V0
  N20: LCD_20_x4.RS, I²C.RS
  N21: LCD_20_x4.R/W, I²C.RW
  N22: LCD_20_x4.E, I²C.E
  N23: LCD_20_x4.DB0, I²C.D0
  N24: LCD_20_x4.DB1, I²C.D1
  N25: LCD_20_x4.DB2, I²C.D2
  N26: LCD_20_x4.DB3, I²C.D3
  N27: LCD_20_x4.DB4, I²C.D4
  N28: LCD_20_x4.DB5, I²C.D5
  N29: LCD_20_x4.DB6, I²C.D6
  N30: LCD_20_x4.DB7, I²C.D7
  N31: LCD_20_x4.LED+, I²C.A
  N32: LCD_20_x4.LED-, I²C.K
  N33: LED1.cathode, R2.Pin_0
  N34: Power_Supply.VCC#5, Relay.power, Elektrisches_Schloss.pin_2
  N35: Power_Supply.GND#11, Relay.ground, Relay.C
  N36: Relay.NC, Elektrisches_Schloss.pin_1

custom parts:
  4x4 Keypad: Matrix membrane keypad 4x4
  LCM1602 IIC: I2C-Module to use a 1602 or 2004 LCD on with the wire.h libory Serial LCD Modul
  YwRobot Breadboard Power Supply: The YwRobot Breadboard Power Supply (MB-V2) has two power rails; they can be 5V or 3V3. Power to the module can be provided through the female USB socket or through the A10 (female) 2.1mm power jack.
  KF-301 Relay: KF-301
